# Fritzing sketch Buehne (saved by Fritzing 1.0.6)

parts:
  U1 = LuaNode32 / ESP32 [part_number=ESP32S-PIN30]
  S1 = Round Pushbutton
  S2 = Round Pushbutton
  S3 = Round Pushbutton
  S4 = Round Pushbutton
  S5 = Round Pushbutton

nets:
  N1: U1.D26, S5.leg1
  N2: U1.D27, S4.leg1
  N3: U1.D14, S3.leg1
  N4: U1.D12, S2.leg1
  N5: U1.D13, S1.leg1
  N6: U1.GND, S1.leg0, S2.leg0, S3.leg0, S4.leg0, S5.leg0

notes:
  3,3V Stepdown
  +
  -

custom parts:
  LuaNode32 / ESP32: New Image for LuaNode32 DOIT ESP32 DEVKIT V1. Base parts from LuaNode32 / ESP32 ESP32 based LuaNode32 by G.Noorlander DOIT Esp32 DevKit v1 (30 pins long, 11 pins width) by Werner Rothschopf (modified by vanepp Dec 2018)
