# Fritzing sketch Regieraum (saved by Fritzing 1.0.6)

parts:
  J1 = double-row-SMD-male-header-16-pins-extended-pads [package=THT]
  U1 = LuaNode32 / ESP32 [part_number=ESP32S-PIN30]

nets:
  N1: J1.pin1, U1.D25
  N2: J1.pin2, U1.D27
  N3: J1.pin3, U1.D14
  N4: J1.pin4, U1.D13
  N5: J1.pin5, U1.D23
  N6: J1.pin6, U1.D5
  N7: J1.pin7, U1.RX2
  N8: J1.pin8, U1.D15
  N9: J1.pin9, J1.pin15, U1.GND
  N10: J1.pin10, U1.D4
  N11: J1.pin11, U1.TX2
  N12: J1.pin12, U1.D19
  N13: J1.pin13, U1.D32
  N14: J1.pin14, U1.D12
  N15: J1.pin16, U1.D26

notes:
  3,3V Stepdown
  +
  -

custom parts:
  double-row-SMD-male-header-16-pins-extended-pads: double row SMD male header extended pads.
  LuaNode32 / ESP32: New Image for LuaNode32 DOIT ESP32 DEVKIT V1. Base parts from LuaNode32 / ESP32 ESP32 based LuaNode32 by G.Noorlander DOIT Esp32 DevKit v1 (30 pins long, 11 pins width) by Werner Rothschopf (modified by vanepp Dec 2018)
